# Fritzing sketch Termidinator (saved by Fritzing 0.9.3b)
breadboards: 1

parts:
  Part1 = Arduino Uno (Rev3)
  S1 = Pushbutton [package="[THT]"]
  S2 = Pushbutton [package="[THT]"]
  S3 = Pushbutton [package="[THT]"]
  S4 = Pushbutton [package="[THT]"]
  S5 = Pushbutton [package="[THT]"]
  S6 = Pushbutton [package="[THT]"]
  S7 = Pushbutton [package="[THT]"]
  S8 = Pushbutton [package="[THT]"]
  S9 = Pushbutton [package="[THT]"]
  R1 = Resistor [tolerance=±1% resistance=220 package=THT]
  R2 = Resistor [tolerance=±1% resistance=220 package=THT]
  R3 = Resistor [tolerance=±1% resistance=220 package=THT]
  R4 = Resistor [tolerance=±1% resistance=220 package=THT]
  R5 = Resistor [tolerance=±1% resistance=220 package=THT]
  R6 = Resistor [tolerance=±1% resistance=220 package=THT]
  R7 = Resistor [tolerance=±1% resistance=220 package=THT]
  R8 = Resistor [tolerance=±1% resistance=220 package=THT]
  R9 = Resistor [tolerance=±1% resistance=220 package=THT]

nets:
  N1: Part1.D8, S5.Pin_1, S5.Pin_2, R5.Pin_0
  N2: Part1.D9_PWM, S6.Pin_1, S6.Pin_2, R6.Pin_0
  N3: Part1.D10_PWM/SS, S7.Pin_1, S7.Pin_2, R7.Pin_0
  N4: Part1.D11_PWM/MOSI, S8.Pin_1, S8.Pin_2, R8.Pin_0
  N5: Part1.D12/MISO, S9.Pin_1, S9.Pin_2, R9.Pin_0
  N6: Part1.D4, S1.Pin_1, S1.Pin_2, R1.Pin_0
  N7: Part1.D5_PWM, S2.Pin_1, S2.Pin_2, R2.Pin_0
  N8: Part1.D6_PWM, S3.Pin_1, S3.Pin_2, R3.Pin_0
  N9: Part1.D7, S4.Pin_1, S4.Pin_2, R4.Pin_0
  N10: Part1.5V, S1.Pin_3, S1.Pin_4, S2.Pin_3, S2.Pin_4, S3.Pin_3, S3.Pin_4, S4.Pin_3, S4.Pin_4, S5.Pin_3, S5.Pin_4, S6.Pin_3, S6.Pin_4, S7.Pin_3, S7.Pin_4, S8.Pin_3, S8.Pin_4, S9.Pin_3, S9.Pin_4, R1.Pin_1, R2.Pin_1, R3.Pin_1, R4.Pin_1, R5.Pin_1, R6.Pin_1, R7.Pin_1, R8.Pin_1, R9.Pin_1
